# Fritzing sketch board (saved by Fritzing 0.9.3b)

parts:
  WeMos_D1_Mini1 = WeMos D1 Mini
  OLED_I2C1 = OLED 128x64 I2C Monochrome Display

nets:
  5V: WeMos_D1_Mini1.5V, OLED_I2C1.VDD
  N1: WeMos_D1_Mini1.D1, OLED_I2C1.SDA
  N2: WeMos_D1_Mini1.D2, OLED_I2C1.SCK
  N3: WeMos_D1_Mini1.G, OLED_I2C1.GND
